# Fritzing sketch PLESCktSchematic_V1 (saved by Fritzing 1.0.5)
# 18650 Li-ion Battery: CC-BY Dr Kristofer Chan, King's College London/Remote-research.org
breadboards: 4

parts:
  Part1 = Arduino Uno (Rev3) - ICSP
  M1 = gear-motor
  M2 = gear-motor
  M3 = gear-motor
  M4 = gear-motor
  U2 = OP27 - Low Noise, Precision Op Amp [part_number=OP27]
  U3 = OP27 - Low Noise, Precision Op Amp [part_number=OP27]
  U4 = OP27 - Low Noise, Precision Op Amp [part_number=OP27]
  U5 = OP27 - Low Noise, Precision Op Amp [part_number=OP27]
  L298N1 = L298N DC motor driver
  BAT1 = 18650 Li-ion Battery [package=battery-18650]
  BAT2 = 18650 Li-ion Battery [package=battery-18650]
  R4 = Resistor [tolerance=±5% resistance=15k package="0402 [SMD]"]
  R3 = Resistor [tolerance=±5% resistance=30k package="0402 [SMD]"]
  R6 = Resistor [tolerance=±5% resistance=15k package="2010 [SMD]"]
  R5 = Resistor [tolerance=±5% resistance=30k package="0402 [SMD]"]
  R8 = Resistor [tolerance=±5% resistance=9k package="2512 [SMD]"]
  R9 = Resistor [tolerance=±5% resistance=10k package="2512 [SMD]"]
  R10 = Resistor [tolerance=±5% resistance=10k package="2512 [SMD]"]
  R11 = Resistor [tolerance=±5% resistance=0.1 power=5W package="2010 [SMD]"]
  R1 = Resistor [tolerance=±5% resistance=0.1 power=5W package="2010 [SMD]"]
  U6 = OP27 - Low Noise, Precision Op Amp [part_number=OP27]
  U7 = OP27 - Low Noise, Precision Op Amp [part_number=OP27]
  C1 = Electrolytic Capacitor [capacitance=1µF voltage=35V package="1010 [SMD, electrolytic]"]
  C2 = Electrolytic Capacitor [capacitance=10µF voltage=35V package="1010 [SMD, electrolytic]"]
  C3 = Electrolytic Capacitor [capacitance=1µF voltage=35V package="1010 [SMD, electrolytic]"]
  R7 = Resistor [tolerance=±5% resistance=1k package="2512 [SMD]"]

nets:
  N1: Part1.A0, U7.-IN, U7.OUT
  N2: Part1.A1, U6.-IN, U6.OUT
  N3: Part1.A4/SDA, U5.-IN, U5.OUT
  N4: Part1.A5/SCL, U2.OUT, R4.Pin_1
  5V: Part1.5V, L298N1.5V
  N5: Part1.GND, U4.+IN, BAT1.-, R6.Pin_0, R9.Pin_1, R11.Pin_0, R1.Pin_0, C3.+, R7.Pin_1
  N6: Part1.D9_PWM, L298N1.ENA
  N7: Part1.D10_PWM/SS, L298N1.ENB
  N8: Part1.D2, L298N1.IN1
  N9: Part1.D3_PWM, L298N1.IN2
  N10: Part1.D4, L298N1.IN3
  N11: Part1.D5_PWM, L298N1.IN4
  N12: Part1.D6_PWM, R8.Pin_0
  N13: M1.pin_1, M2.pin_1, L298N1.OUT3
  N14: M1.pin_2, M2.pin_2, L298N1.OUT4
  N15: M3.pin_1, M4.pin_1, L298N1.OUT2
  N16: M3.pin_2, M4.pin_2, L298N1.OUT1
  N17: U2.-IN, R4.Pin_0, R5.Pin_0
  N18: U2.+IN, R3.Pin_0, R6.Pin_1
  N19: U3.-IN, U3.OUT, R3.Pin_1
  N20: U3.+IN, L298N1.12V, BAT2.+, R11.Pin_1, U7.+IN, C1.-, C2.-
  N21: U4.-IN, U4.OUT, R5.Pin_1
  N22: U5.+IN, L298N1.GND, R1.Pin_1
  N23: BAT1.+, BAT2.-
  N24: R8.Pin_1, R10.Pin_0, R7.Pin_0
  N25: R9.Pin_0, U6.+IN, C1.+
  N26: R10.Pin_1, C2.+, C3.-

custom parts:
  L298N DC motor driver: 2x DC motor driver with 78M05 positive voltage regulator (7..35 V) L298N: max 46 V, 2 A Set 5 V Enable jumper to enable 5 V regultor (needed for the L298N) and +5 V output at screw terminal or supply external +5 V at screw terminal Set ENA and/or ENB to +5 V to enable motor permanently or supply ENA and/or ENB with PWM signal IN1 and IN2 set rotation directory for motor A (OUT1/OUT2) IN2 and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
  18650 Li-ion Battery: 18650 li-ion Battery Standard 18650 battery with interactive connectors Creative Common Attribution 4.0 International (CC-BY 4.0) license. Any use of this part requires attribution of Dr Kristofer Chan, Department of Geography, King's College London. Contact kristofer.chan [at] kcl.ac.uk OR kris [at] remote-research.org for further information.
